// Logisim project s-mips.circ as structural Verilog: 22 circuits, main circuit S-MIPS Board
module S_MIPS_Board (
  input  DESHABILITAR_DISPATCHER,
  output halt
);

  wire button_1_out, CLK, CS, d_ff_1_q, LCLR, LoadRAM, LoadRAMOn, LW, R_R_W, R_W, ram_dispatcher_1_finished,
       RCS, Reset_out, RST, TTY_EN;
  wire [2:0] KDB;
  wire [3:0] LMask, Mask, ram_1_read_time, ram_1_write_time, RMask;
  wire [6:0] KDB_DATA, TTY_DATA;
  wire [15:0] Addr, LAddr, RAddr;
  wire [31:0] I0, I1, I2, I3, LData, ram_1_data_out_0, ram_1_data_out_1, ram_1_data_out_2, ram_1_data_out_3,
       RI0, RI1, RI2, RI3;

  TTY #(.rows(25), .cols(80)) tty_1 (.data(TTY_DATA), .clk(CLK), .we(TTY_EN), .clr(RST));
  not not_1 (LoadRAMOn, ram_dispatcher_1_finished);
  RAM_Dispatcher ram_dispatcher_1 (
    .WriteTime(ram_1_write_time), .Clock(CLK), .Data(LData), .Address(LAddr), .Mask(LMask),
    .Finished(ram_dispatcher_1_finished), .Write(LW), .CLR(LCLR));
  Keyboard #(.buflen(64)) keyboard_1 (.clk(CLK), .re(KDB[0]), .avail(KDB[2]), .data(KDB_DATA));  // open: clr
  RAM ram_1 (
    .Address(RAddr), .Data_Out_0(ram_1_data_out_0), .Data_Out_1(ram_1_data_out_1),
    .Data_Out_2(ram_1_data_out_2), .Data_Out_3(ram_1_data_out_3), .Data_In_0(RI0), .Data_In_1(RI1),
    .Data_In_2(RI2), .Data_In_3(RI3), .Mask(RMask), .nRead_Write(R_R_W), .Chip_Select(RCS),
    .Read_Time(ram_1_read_time), .Reset(button_1_out), .Write_Time(ram_1_write_time));
  Button button_1 (.out(button_1_out));
  D_Flip_Flop d_ff_1 (.clk(CLK), .D(1'b1), .Q(d_ff_1_q), .reset(Reset_out));  // open: Qn, preset, en
  Button Reset (.out(Reset_out));
  S_MIPS s_mips_1 (
    .Kbd_Enable(KDB[0]), .Address(Addr), .Kbd_Clear(KDB[1]), .Kbd_Available(KDB[2]), .RAM_In_0(I0),
    .Kbd_ASCII_Data(KDB_DATA), .RAM_In_1(I1), .TTY_Enable(TTY_EN), .RAM_In_2(I2), .RAM_In_3(I3),
    .TTY_ASCII_Data(TTY_DATA), .Reset(RST), .RAM_Out_0(ram_1_data_out_0), .Clock(CLK),
    .RAM_Out_1(ram_1_data_out_1), .Stop(halt), .RAM_Out_2(ram_1_data_out_2), .RAM_Out_3(ram_1_data_out_3),
    .Mask(Mask), .Read_Time(ram_1_read_time), .Write_Time(ram_1_write_time), .nRead_Write(R_W),
    .Chip_Select(CS));
  D_Flip_Flop d_ff_2 (.clk(CLK), .D(d_ff_1_q), .Qn(LCLR), .reset(Reset_out));  // open: Q, preset, en
  or or_1 (RST, LCLR, LoadRAM);
  Clock clock_1 (.out(CLK));
  Multiplexer #(.width(32), .enable("false")) multiplexer_1 (.in0(I0), .in1(LData), .out(RI0), .sel(LoadRAM));
  Multiplexer #(.width(32), .enable("false")) multiplexer_2 (.in0(I1), .in1(LData), .out(RI1), .sel(LoadRAM));
  Multiplexer #(.width(32), .enable("false")) multiplexer_3 (.in0(I2), .in1(LData), .out(RI2), .sel(LoadRAM));
  Multiplexer #(.width(32), .enable("false")) multiplexer_4 (.in0(I3), .in1(LData), .out(RI3), .sel(LoadRAM));
  and and_1 (LoadRAM, ~DESHABILITAR_DISPATCHER, LoadRAMOn);  // AND_Gate
  Multiplexer #(.width(16), .enable("false")) multiplexer_5 (.in0(Addr), .in1(LAddr), .out(RAddr), .sel(LoadRAM));
  Multiplexer #(.width(4), .enable("false")) multiplexer_6 (.in0(Mask), .in1(LMask), .out(RMask), .sel(LoadRAM));
  Multiplexer #(.enable("false")) multiplexer_7 (.in0(CS), .in1(LW), .out(RCS), .sel(LoadRAM));
  Multiplexer #(.enable("false")) multiplexer_8 (.in0(R_W), .in1(LW), .out(R_R_W), .sel(LoadRAM));

  // Notes on the sheet:
  //   NO MODIFICAR
  //   Keyboard
endmodule

module RAM (
  input  [15:0] Address,
  input  [31:0] Data_In_0,
  input  [31:0] Data_In_1,
  input  [31:0] Data_In_2,
  input  [31:0] Data_In_3,
  input  [3:0] Mask,
  input  nRead_Write,
  input  Chip_Select,
  input  Reset,
  output [31:0] Data_Out_0,
  output [31:0] Data_Out_1,
  output [31:0] Data_Out_2,
  output [31:0] Data_Out_3,
  output [3:0] Read_Time,
  output [3:0] Write_Time
);

  wire and_2_out, and_3_out, and_4_out, and_5_out, and_6_out, and_7_out, and_8_out, and_9_out, Changed, CLK,
       comparator_2_eq, comparator_3_eq, comparator_4_eq, comparator_5_eq, comparator_6_eq, Count,
       demultiplexer_3_out0, Idle, Idle_q, Load, Load0, Load1, nand_1_out, or_1_out, or_2_out, or_3_out,
       or_4_out, or_5_out, or_6_out, or_7_out, or_8_out, or_9_out, or_10_out, Proc_q, Update_Mem, Zero_Time;
  wire [3:0] counter_1_q, multiplexer_1_out, subtractor_1_out;
  wire [31:0] register_1_q, register_2_q, register_3_q, register_4_q, register_5_q;

  // Probe on 4'b0011
  // Probe on 4'b0010
  Multiplexer #(.width(4), .enable("false")) multiplexer_1 (
    .in0(4'b0011), .in1(4'b0010), .out(multiplexer_1_out), .sel(nRead_Write));
  or or_1 (or_1_out, Idle, Update_Mem);
  or or_2 (or_2_out, ~Chip_Select, Reset);  // OR_Gate
  Subtractor #(.width(4)) subtractor_1 (.a(multiplexer_1_out), .b(4'b0010), .out(subtractor_1_out));  // open: bin, bout
  Demultiplexer #(.enable("false")) demultiplexer_1 (.out0(Idle), .out1(Load0), .in(Idle_q), .sel(Changed));
  D_Flip_Flop u_Idle (.clk(CLK), .D(or_1_out), .Q(Idle_q), .preset(or_2_out));  // open: Qn, en, reset
  // Probe on counter_1_q
  Counter #(.width(4), .max('hf)) counter_1 (
    .load(Load), .D(subtractor_1_out), .count(Count), .Q(counter_1_q), .clk(CLK), .clr(or_3_out));  // open: carry
  or or_3 (or_3_out, ~Chip_Select, Reset);  // OR_Gate
  Comparator #(.width(4), .mode("unsigned")) comparator_1 (
    .a(4'b0000), .b(counter_1_q), .eq(Zero_Time));  // open: gt, lt
  or or_4 (or_4_out, Count, Load0, Load1);
  Register #(.width(32)) register_1 (.D(Data_In_0), .en(Chip_Select), .Q(register_1_q), .clk(CLK), .clr(or_5_out));
  or or_5 (or_5_out, ~Chip_Select, Reset);  // OR_Gate
  Register #(.width(32)) register_2 (.D(Data_In_1), .en(Chip_Select), .Q(register_2_q), .clk(CLK), .clr(or_6_out));
  or or_6 (or_6_out, ~Chip_Select, Reset);  // OR_Gate
  Register #(.width(32)) register_3 (.D(Data_In_2), .en(Chip_Select), .Q(register_3_q), .clk(CLK), .clr(or_7_out));
  or or_7 (or_7_out, ~Chip_Select, Reset);  // OR_Gate
  Register #(.width(32)) register_4 (.D(Data_In_3), .en(Chip_Select), .Q(register_4_q), .clk(CLK), .clr(or_8_out));
  or or_8 (or_8_out, ~Chip_Select, Reset);  // OR_Gate
  Register #(.width(32)) register_5 (
    .D({{11{1'b1}}, nRead_Write, Mask, Address}), .en(Chip_Select), .Q(register_5_q), .clk(CLK),
    .clr(or_9_out));
  or or_9 (or_9_out, ~Chip_Select, Reset);  // OR_Gate
  D_Flip_Flop Proc (.clk(CLK), .D(or_4_out), .Q(Proc_q), .reset(or_10_out));  // open: Qn, preset, en
  or or_10 (or_10_out, ~Chip_Select, Reset);  // OR_Gate
  Demultiplexer #(.enable("false")) demultiplexer_2 (
    .out0(Count), .out1(Update_Mem), .in(demultiplexer_3_out0), .sel(Zero_Time));
  Demultiplexer #(.enable("false")) demultiplexer_3 (
    .out0(demultiplexer_3_out0), .out1(Load1), .in(Proc_q), .sel(Changed));
  Clock clock_1 (.out(CLK));
  Comparator #(.width(32)) comparator_2 (.a(register_1_q), .b(Data_In_0), .eq(comparator_2_eq));  // open: gt, lt
  Comparator #(.width(32)) comparator_3 (.a(register_2_q), .b(Data_In_1), .eq(comparator_3_eq));  // open: gt, lt
  Comparator #(.width(32)) comparator_4 (.a(register_3_q), .b(Data_In_2), .eq(comparator_4_eq));  // open: gt, lt
  Comparator #(.width(32)) comparator_5 (.a(register_4_q), .b(Data_In_3), .eq(comparator_5_eq));  // open: gt, lt
  Comparator #(.width(32)) comparator_6 (
    .a(register_5_q), .b({{11{1'b1}}, nRead_Write, Mask, Address}), .eq(comparator_6_eq));  // open: gt, lt
  nand nand_1 (nand_1_out, comparator_6_eq, comparator_2_eq, comparator_3_eq, comparator_4_eq, comparator_5_eq);
  and and_1 (Changed, nand_1_out, Chip_Select);
  or or_11 (Load, Count, Load1, Load0);
  and and_2 (and_2_out, Mask[0], Update_Mem, nRead_Write);
  and and_3 (and_3_out, Mask[1], Update_Mem, nRead_Write);
  and and_4 (and_4_out, Mask[2], Update_Mem, nRead_Write);
  and and_5 (and_5_out, Mask[3], Update_Mem, nRead_Write);
  RAM_part #(.addrWidth(16), .dataWidth(32), .bus("separate")) ram_1 (
    .addr(Address), .din(Data_In_0), .data(Data_Out_0), .str(and_2_out), .sel(Chip_Select), .clk(CLK),
    .ld(and_6_out), .clr(Reset));
  and and_6 (and_6_out, ~nRead_Write, Idle);  // AND_Gate
  RAM_part #(.addrWidth(16), .dataWidth(32), .bus("separate")) ram_2 (
    .addr(Address), .din(Data_In_1), .data(Data_Out_1), .str(and_3_out), .sel(Chip_Select), .clk(CLK),
    .ld(and_7_out), .clr(Reset));
  and and_7 (and_7_out, ~nRead_Write, Idle);  // AND_Gate
  RAM_part #(.addrWidth(16), .dataWidth(32), .bus("separate")) ram_3 (
    .addr(Address), .din(Data_In_2), .data(Data_Out_2), .str(and_4_out), .sel(Chip_Select), .clk(CLK),
    .ld(and_8_out), .clr(Reset));
  and and_8 (and_8_out, ~nRead_Write, Idle);  // AND_Gate
  RAM_part #(.addrWidth(16), .dataWidth(32), .bus("separate")) ram_4 (
    .addr(Address), .din(Data_In_3), .data(Data_Out_3), .str(and_5_out), .sel(Chip_Select), .clk(CLK),
    .ld(and_9_out), .clr(Reset));
  and and_9 (and_9_out, ~nRead_Write, Idle);  // AND_Gate

  assign Read_Time = 4'b0011;
  assign Write_Time = 4'b0010;

  // Other names for the same wires on the sheet: M0 = Mask[0]; M1 = Mask[1]; M2 = Mask[2]; M3 = Mask[3];
  //   RW = nRead_Write; CLR = Reset; CS = Chip_Select; Load2 = Count

  // Notes on the sheet:
  //   NO MODIFICAR
  //   excepto quizás los valores RT y WT
  //   BANK0
  //   BANK1
  //   BANK2
  //   BANK3
endmodule

module RAM_Dispatcher (
  input  [3:0] WriteTime,
  input  Clock,
  input  CLR,
  output [31:0] Data,
  output [15:0] Address,
  output [3:0] Mask,
  output Finished,
  output Write
);

  wire demultiplexer_2_out1, demultiplexer_3_out1, End, IDLE_q, IncAddr, Load, or_1_out, or_2_out, While_q,
       WriteEnd;
  wire [3:0] counter_1_q;
  wire [31:0] CurrentAddress_q;

  Counter #(.width(32), .max('hffffffff)) CurrentAddress (
    .count(IncAddr), .Q({CurrentAddress_q[31:18], Address, CurrentAddress_q[1:0]}), .clk(Clock), .clr(CLR));  // open: load, D, carry
  or or_1 (or_1_out, IncAddr, demultiplexer_3_out1, Finished);
  D_Flip_Flop IDLE (.clk(Clock), .D(or_1_out), .Q(IDLE_q), .preset(CLR));  // open: Qn, en, reset
  Demultiplexer #(.enable("false")) demultiplexer_1 (.out0(Load), .out1(Finished), .in(IDLE_q), .sel(End));
  D_Flip_Flop While (.clk(Clock), .D(or_2_out), .Q(While_q), .reset(CLR));  // open: Qn, preset, en
  or or_2 (or_2_out, Write, Load);
  RAM_part #(.addrWidth(18), .dataWidth(32)) ram_1 (
    .addr({Address, CurrentAddress_q[1:0]}), .data(Data), .clk(Clock));  // open: sel, ld, clr
  Demultiplexer #(.enable("false")) demultiplexer_2 (
    .out0(Write), .out1(demultiplexer_2_out1), .in(While_q), .sel(WriteEnd));
  Decoder_part #(.select(2)) decoder_1 (
    .out0(Mask[0]), .out1(Mask[1]), .out2(Mask[2]), .out3(Mask[3]), .sel(CurrentAddress_q[1:0]));  // open: en
  Demultiplexer #(.enable("false")) demultiplexer_3 (
    .out0(IncAddr), .out1(demultiplexer_3_out1), .in(demultiplexer_2_out1), .sel(End));
  Counter #(.width(4), .max('hf)) counter_1 (
    .load(Load), .D(WriteTime), .count(Write), .Q(counter_1_q), .clk(Clock));  // open: carry, clr
  Comparator #(.width(32)) comparator_1 (.a(Data), .b({32{1'b1}}), .eq(End));  // open: gt, lt
  Comparator #(.width(4)) comparator_2 (.a(4'b0000), .b(counter_1_q), .eq(WriteEnd));  // open: gt, lt

  // Other names for the same wires on the sheet: CLK = Clock; Count = Write; WT[3:0] = WriteTime
endmodule

module S_MIPS (
  input  Kbd_Available,
  input  [6:0] Kbd_ASCII_Data,
  input  [31:0] RAM_Out_0,
  input  [31:0] RAM_Out_1,
  input  Reset,
  input  [31:0] RAM_Out_2,
  input  Clock,
  input  [31:0] RAM_Out_3,
  input  [3:0] Read_Time,
  input  [3:0] Write_Time,
  output Kbd_Enable,
  output [15:0] Address,
  output Kbd_Clear,
  output TTY_Enable,
  output [6:0] TTY_ASCII_Data,
  output Stop,
  output [31:0] RAM_In_0,
  output [31:0] RAM_In_1,
  output [31:0] RAM_In_2,
  output [31:0] RAM_In_3,
  output [3:0] Mask,
  output nRead_Write,
  output Chip_Select
);

  wire alu_1_condition, decoder_1_activate_alu, decoder_1_hilo_select, decoder_1_hilo_write,
       decoder_1_r_write, decoder_1_sp_write, io_bridge_1_ready;
  wire [3:0] decoder_1_alu_code, decoder_1_io_code;
  wire [4:0] decoder_1_s_r1, decoder_1_s_r2, decoder_1_s_r3;
  wire [31:0] alu_1_result_1, alu_1_result_2, decoder_1_io_address, decoder_1_io_output, decoder_1_op1,
       decoder_1_op2, decoder_1_r3, decoder_1_r4, decoder_1_sp_out, io_bridge_1_output,
       registryfile_1_hilo_output, registryfile_1_r1, registryfile_1_r2, registryfile_1_sp_out;

  IO_Bridge io_bridge_1 (
    .Clock(Clock), .Reset(Reset), .RAM0_Read(RAM_Out_0), .RAM1_Read(RAM_Out_1), .RAM2_Read(RAM_Out_2),
    .RAM3_Read(RAM_Out_3), .RAM0_Write(RAM_In_0), .RAM1_Write(RAM_In_1), .RAM2_Write(RAM_In_2),
    .RAM3_Write(RAM_In_3), .RAM_Address(Address), .Read_Time(Read_Time), .Write_Time(Write_Time),
    .Write_Mask(Mask), .RAM_ON(Chip_Select), .RAM_R_W(nRead_Write), .KBD_Data(Kbd_ASCII_Data),
    .KBD_Avail(Kbd_Available), .KBD_On(Kbd_Enable), .TTY_Data(TTY_ASCII_Data), .TTY_On(TTY_Enable),
    .Code(decoder_1_io_code), .Address(decoder_1_io_address), .Input(decoder_1_io_output),
    .Output(io_bridge_1_output), .Ready(io_bridge_1_ready));
  Decoder decoder_1 (
    .Clock(Clock), .Ready(io_bridge_1_ready), .IO_Code(decoder_1_io_code), .IO_Address(decoder_1_io_address),
    .IO_Output(decoder_1_io_output), .IO_Input(io_bridge_1_output), .Reset(Reset),
    .SP_IN(registryfile_1_sp_out), .SP_OUT(decoder_1_sp_out), .SP_write(decoder_1_sp_write),
    .ALU_code(decoder_1_alu_code), .Activate_ALU(decoder_1_activate_alu), .OP1(decoder_1_op1),
    .OP2(decoder_1_op2), .Result_1(alu_1_result_1), .Result_2(alu_1_result_2), .Condition(alu_1_condition),
    .Halt(Stop), .R1(registryfile_1_r1), .R2(registryfile_1_r2), .R3(decoder_1_r3), .S_R1(decoder_1_s_r1),
    .S_R2(decoder_1_s_r2), .S_R3(decoder_1_s_r3), .R_Write(decoder_1_r_write), .R4(decoder_1_r4),
    .HiLo_write(decoder_1_hilo_write), .HiLo_select(decoder_1_hilo_select),
    .HiLo_read(registryfile_1_hilo_output));  // open: Invalid
  ALU alu_1 (
    .Enable(decoder_1_activate_alu), .Code(decoder_1_alu_code), .OP1(decoder_1_op1), .OP2(decoder_1_op2),
    .Result_1(alu_1_result_1), .Result_2(alu_1_result_2), .Condition(alu_1_condition));
  RegistryFile registryfile_1 (
    .Clock(Clock), .S_R1(decoder_1_s_r1), .S_R2(decoder_1_s_r2), .Modify(decoder_1_s_r3),
    .New_Value(decoder_1_r3), .Write(decoder_1_r_write), .Reset(Reset), .R4(decoder_1_r4),
    .Write_HiLo(decoder_1_hilo_write), .Select_HiLo(decoder_1_hilo_select),
    .HiLo_output(registryfile_1_hilo_output), .R1(registryfile_1_r1), .R2(registryfile_1_r2),
    .SP_OUT(registryfile_1_sp_out), .SP_IN(decoder_1_sp_out), .SP_write(decoder_1_sp_write));

  // Other names for the same wires on the sheet: CLK = Clock; CLR = Reset; KBD_AVAIL = Kbd_Available;
  //   KBD_CLR = Kbd_Clear; KBD_DATA[6:0] = Kbd_ASCII_Data; TTY_DATA[6:0] = TTY_ASCII_Data

  // Notes on the sheet:
  //   RAM ADDRESS
  //   KEYBOARD
  //   TTY
  //   SEQUENCING
endmodule

module ALU_2Complement (
  input  [31:0] OP,
  output [31:0] Result
);

  wire [31:0] not_1_out;

  assign not_1_out = ~OP;  // NOT_Gate not_1, 32 bits wide
  Adder #(.width(32)) adder_1 (.a(not_1_out), .b(32'h1), .out(Result));  // open: cin, cout
endmodule

module ALU_2Complement64 (
  input  [31:0] OP_Hi,
  input  [31:0] OP_Lo,
  output [31:0] Result_Hi,
  output [31:0] Result_Lo
);

  wire adder_2_cout;
  wire [31:0] not_1_out, not_2_out;

  assign not_1_out = ~OP_Hi;  // NOT_Gate not_1, 32 bits wide
  assign not_2_out = ~OP_Lo;  // NOT_Gate not_2, 32 bits wide
  Adder #(.width(32)) adder_1 (.a(not_1_out), .b(32'h1), .out(Result_Hi), .cin(adder_2_cout));  // open: cout
  Adder #(.width(32)) adder_2 (.a(not_2_out), .b(32'h1), .out(Result_Lo), .cout(adder_2_cout));  // open: cin
endmodule

module ALU_Divisor (
  input  [31:0] OP1,
  input  [31:0] OP2,
  output [31:0] Result_Hi,
  output [31:0] Result_Lo
);

  wire or_1_out;
  wire [1:1] xor_1_out;
  wire [31:0] adder_1_out, alu_2complement_1_result, alu_2complement_2_result, alu_2complement_3_result,
       divider_1_out, divider_1_rem, multiplexer_1_out, multiplexer_2_out, multiplexer_4_out,
       subtractor_1_out, subtractor_2_out;

  Multiplexer #(.width(32), .disabled(0), .enable("false")) multiplexer_1 (
    .in0(OP1), .in1(alu_2complement_1_result), .out(multiplexer_1_out), .sel(OP1[31]));
  ALU_2Complement alu_2complement_1 (.OP(OP1), .Result(alu_2complement_1_result));
  Multiplexer #(.width(32), .disabled(0), .enable("false")) multiplexer_2 (
    .in0(OP2), .in1(alu_2complement_2_result), .out(multiplexer_2_out), .sel(OP2[31]));
  ALU_2Complement alu_2complement_2 (.OP(OP2), .Result(alu_2complement_2_result));
  Divider #(.width(32)) divider_1 (
    .a(multiplexer_1_out), .b(multiplexer_2_out), .out(divider_1_out), .rem(divider_1_rem));  // open: upper
  or or_1 (or_1_out, OP1[31], OP2[31]);
  Subtractor #(.width(32)) subtractor_1 (
    .a(multiplexer_2_out), .b(divider_1_rem), .out(subtractor_1_out));  // open: bin, bout
  xor xor_1 (xor_1_out[1], OP1[31], OP2[31]);
  Multiplexer #(.width(32), .disabled(0), .enable("false")) multiplexer_3 (
    .in0(divider_1_rem), .in1(subtractor_1_out), .out(Result_Hi), .sel(or_1_out));
  Multiplexer #(.width(32), .disabled(0), .enable("false")) multiplexer_4 (
    .in0(divider_1_out), .in1(alu_2complement_3_result), .out(multiplexer_4_out), .sel(xor_1_out[1]));
  ALU_2Complement alu_2complement_3 (.OP(divider_1_out), .Result(alu_2complement_3_result));
  Subtractor #(.width(32)) subtractor_2 (.a(multiplexer_4_out), .b(32'h1), .out(subtractor_2_out));  // open: bin, bout
  Adder #(.width(32)) adder_1 (.a(multiplexer_4_out), .b(32'h1), .out(adder_1_out));  // open: cin, cout
  Multiplexer #(.select(2), .width(32), .disabled(0), .enable("false")) multiplexer_5 (
    .in0(multiplexer_4_out), .in1(adder_1_out), .in2(subtractor_2_out), .in3(subtractor_2_out),
    .out(Result_Lo), .sel({xor_1_out[1], OP2[31]}));
endmodule

module ALU_Multiplier (
  input  [31:0] OP1,
  input  [31:0] OP2,
  output [31:0] Result_Hi,
  output [31:0] Result_Lo
);

  wire xor_1_out;
  wire [31:0] alu_2complement64_1_result_hi, alu_2complement64_1_result_lo, alu_2complement_1_result,
       alu_2complement_2_result, multiplexer_1_out, multiplexer_2_out, multiplier_1_cout, multiplier_1_out;

  Multiplexer #(.width(32), .disabled(0), .enable("false")) multiplexer_1 (
    .in0(OP1), .in1(alu_2complement_1_result), .out(multiplexer_1_out), .sel(OP1[31]));
  ALU_2Complement alu_2complement_1 (.OP(OP1), .Result(alu_2complement_1_result));
  Multiplexer #(.width(32), .disabled(0), .enable("false")) multiplexer_2 (
    .in0(OP2), .in1(alu_2complement_2_result), .out(multiplexer_2_out), .sel(OP2[31]));
  ALU_2Complement alu_2complement_2 (.OP(OP2), .Result(alu_2complement_2_result));
  Multiplier #(.width(32)) multiplier_1 (
    .a(multiplexer_1_out), .b(multiplexer_2_out), .out(multiplier_1_out), .cout(multiplier_1_cout));  // open: cin
  xor xor_1 (xor_1_out, OP1[31], OP2[31]);
  ALU_2Complement64 alu_2complement64_1 (
    .OP_Hi(multiplier_1_cout), .OP_Lo(multiplier_1_out), .Result_Hi(alu_2complement64_1_result_hi),
    .Result_Lo(alu_2complement64_1_result_lo));
  Multiplexer #(.width(32), .disabled(0), .enable("false")) multiplexer_3 (
    .in0(multiplier_1_cout), .in1(alu_2complement64_1_result_hi), .out(Result_Hi), .sel(xor_1_out));
  Multiplexer #(.width(32), .disabled(0), .enable("false")) multiplexer_4 (
    .in0(multiplier_1_out), .in1(alu_2complement64_1_result_lo), .out(Result_Lo), .sel(xor_1_out));
endmodule

module ALU (
  input  Enable,
  input  [3:0] Code,
  input  [31:0] OP1,
  input  [31:0] OP2,
  output [31:0] Result_1,
  output [31:0] Result_2,
  output Condition
);

  wire comparator_1_lt, comparator_2_eq, comparator_2_lt, comparator_3_eq, comparator_3_gt, comparator_3_lt,
       or_2_out;
  wire [0:0] adder_1_cout, subtractor_1_bout;
  wire [31:0] adder_1_out, alu_divisor_1_result_hi, alu_divisor_1_result_lo, alu_multiplier_1_result_hi,
       alu_multiplier_1_result_lo, and_1_out, divider_1_out, divider_1_rem, multiplexer_1_out,
       multiplexer_3_out, multiplier_1_cout, multiplier_1_out, not_1_out, or_1_out, subtractor_1_out,
       xor_1_out;

  Adder #(.width(32)) adder_1 (.a(OP1), .b(OP2), .out(adder_1_out), .cout(adder_1_cout[0]));  // open: cin
  Subtractor #(.width(32)) subtractor_1 (
    .a(OP1), .b(OP2), .out(subtractor_1_out), .bout(subtractor_1_bout[0]));  // open: bin
  assign and_1_out = OP1 & OP2;  // AND_Gate and_1, 32 bits wide
  assign or_1_out = OP1 | OP2;  // OR_Gate or_1, 32 bits wide
  assign not_1_out = ~or_1_out;  // NOT_Gate not_1, 32 bits wide
  assign xor_1_out = OP1 ^ OP2;  // XOR_Gate xor_1, 32 bits wide
  ALU_Multiplier alu_multiplier_1 (
    .OP1(OP1), .OP2(OP2), .Result_Hi(alu_multiplier_1_result_hi), .Result_Lo(alu_multiplier_1_result_lo));
  Multiplier #(.width(32)) multiplier_1 (
    .a(OP1), .b(OP2), .out(multiplier_1_out), .cout(multiplier_1_cout));  // open: cin
  ALU_Divisor alu_divisor_1 (
    .OP1(OP1), .OP2(OP2), .Result_Hi(alu_divisor_1_result_hi), .Result_Lo(alu_divisor_1_result_lo));
  Divider #(.width(32)) divider_1 (.a(OP1), .b(OP2), .out(divider_1_out), .rem(divider_1_rem));  // open: upper
  Multiplexer #(.width(32), .disabled(0), .enable("false")) multiplexer_1 (
    .in0({32{1'b0}}), .in1(32'h1), .out(multiplexer_1_out), .sel(comparator_1_lt));
  Comparator #(.width(32)) comparator_1 (.a(OP1), .b(OP2), .lt(comparator_1_lt));  // open: gt, eq
  Comparator #(.width(32), .mode("unsigned")) comparator_2 (
    .a(OP1), .b(OP2), .eq(comparator_2_eq), .lt(comparator_2_lt));  // open: gt
  Comparator #(.width(32)) comparator_3 (
    .a(OP1), .b({32{1'b0}}), .gt(comparator_3_gt), .eq(comparator_3_eq), .lt(comparator_3_lt));
  Multiplexer #(.select(4), .width(32), .disabled(0)) multiplexer_2 (
    .in0(adder_1_out), .in1(subtractor_1_out), .in2(and_1_out), .in3(or_1_out), .in4(not_1_out),
    .in5(xor_1_out), .in6(alu_multiplier_1_result_lo), .in7(multiplier_1_out), .in8(alu_divisor_1_result_lo),
    .in9(divider_1_out), .in10(multiplexer_1_out), .in11(multiplexer_3_out), .in12({32{1'b0}}),
    .in13({32{1'b0}}), .in14({32{1'b0}}), .in15({32{1'b0}}), .out(Result_1), .sel(Code), .en(Enable));
  Multiplexer #(.width(32), .disabled(0), .enable("false")) multiplexer_3 (
    .in0({32{1'b0}}), .in1(32'h1), .out(multiplexer_3_out), .sel(comparator_2_lt));
  Multiplexer #(.select(4), .width(32), .disabled(0)) multiplexer_4 (
    .in0({{31{1'b0}}, adder_1_cout[0]}), .in1({{31{1'b0}}, subtractor_1_bout[0]}), .in2({32{1'b0}}),
    .in3({32{1'b0}}), .in4({32{1'b0}}), .in5({32{1'b0}}), .in6(alu_multiplier_1_result_hi),
    .in7(multiplier_1_cout), .in8(alu_divisor_1_result_hi), .in9(divider_1_rem), .in10({32{1'b0}}),
    .in11({32{1'b0}}), .in12({32{1'b0}}), .in13({32{1'b0}}), .in14({32{1'b0}}), .in15({32{1'b0}}),
    .out(Result_2), .sel(Code), .en(Enable));
  Multiplexer #(.select(4), .disabled(0)) multiplexer_5 (
    .in0(1'b0), .in1(1'b0), .in2(1'b0), .in3(1'b0), .in4(1'b0), .in5(1'b0), .in6(1'b0), .in7(1'b0),
    .in8(1'b0), .in9(1'b0), .in10(1'b0), .in11(1'b0), .in12(comparator_2_eq), .in13(or_2_out),
    .in14(comparator_3_gt), .in15(comparator_3_lt), .out(Condition), .sel(Code), .en(Enable));
  or or_2 (or_2_out, comparator_3_eq, comparator_3_lt);
endmodule

module Decoder_Branch (
  input  Enable,
  input  d,
  input  e,
  input  f,
  output Invalid,
  output bltz,
  output beq,
  output bne,
  output blez,
  output bgtz
);

  wire decoder_1_out0, decoder_1_out2, decoder_1_out3;

  Decoder_part #(.select(3), .disabled(0)) decoder_1 (
    .out0(decoder_1_out0), .out1(bltz), .out2(decoder_1_out2), .out3(decoder_1_out3), .out4(beq), .out5(bne),
    .out6(blez), .out7(bgtz), .sel({d, e, f}), .en(Enable));
  or or_1 (Invalid, decoder_1_out0, decoder_1_out2, decoder_1_out3);
endmodule

module Decoder_Functions (
  input  Enable,
  input  a,
  input  b,
  input  c,
  input  d,
  input  e,
  input  f,
  output Invalid,
  output add,
  output sub,
  output \and ,
  output \or ,
  output \nor ,
  output \xor ,
  output mul,
  output mulu,
  output div,
  output divu,
  output slt,
  output sltu,
  output mfhi,
  output mflo,
  output jr
);

  wire and_1_out, decoder_1_out0, decoder_1_out1, decoder_1_out2, decoder_1_out3, decoder_1_out5,
       decoder_1_out6, decoder_1_out7, decoder_2_out3, decoder_2_out4, decoder_2_out6, decoder_3_out1,
       decoder_3_out3, decoder_3_out4, decoder_3_out5, decoder_3_out7, decoder_4_out1, decoder_4_out3,
       decoder_4_out4, decoder_4_out5, decoder_4_out6, decoder_4_out7, decoder_5_out1, decoder_5_out3,
       decoder_5_out5, decoder_5_out7, or_1_out, or_3_out, or_4_out, or_5_out, or_6_out, or_7_out, or_8_out;
  wire [2:0] buffer_1_out;

  Decoder_part #(.select(3), .disabled(0)) decoder_1 (
    .out0(decoder_1_out0), .out1(decoder_1_out1), .out2(decoder_1_out2), .out3(decoder_1_out3), .out4(jr),
    .out5(decoder_1_out5), .out6(decoder_1_out6), .out7(decoder_1_out7), .sel({c, b, a}), .en(Enable));
  or or_1 (or_1_out, jr, decoder_1_out0);
  or or_2 (Invalid, and_1_out, decoder_1_out3, decoder_1_out7, or_3_out);
  or or_3 (or_3_out, or_5_out, or_6_out, decoder_2_out3, decoder_2_out4, decoder_2_out6);
  assign buffer_1_out = {f, e, d};  // Buffer buffer_1, 3 bits wide
  and and_1 (and_1_out, or_1_out, or_4_out);
  or or_4 (or_4_out, buffer_1_out[2], buffer_1_out[1], buffer_1_out[0]);
  or or_5 (or_5_out, decoder_4_out1, decoder_4_out3, decoder_4_out4, decoder_4_out5, decoder_4_out6, decoder_4_out7, or_7_out);
  Decoder_part #(.select(3), .disabled(0)) decoder_2 (
    .out0(add), .out1(\and ), .out2(sub), .out3(decoder_2_out3), .out4(decoder_2_out4), .out5(\or ),
    .out6(decoder_2_out6), .out7(\nor ), .sel({f, e, d}), .en(decoder_1_out1));
  Decoder_part #(.select(3), .disabled(0)) decoder_3 (
    .out0(\xor ), .out1(decoder_3_out1), .out2(slt), .out3(decoder_3_out3), .out4(decoder_3_out4),
    .out5(decoder_3_out5), .out6(sltu), .out7(decoder_3_out7), .sel({f, e, d}), .en(decoder_1_out5));
  Decoder_part #(.select(3), .disabled(0)) decoder_4 (
    .out0(mfhi), .out1(decoder_4_out1), .out2(mflo), .out3(decoder_4_out3), .out4(decoder_4_out4),
    .out5(decoder_4_out5), .out6(decoder_4_out6), .out7(decoder_4_out7), .sel({f, e, d}), .en(decoder_1_out2));
  Decoder_part #(.select(3), .disabled(0)) decoder_5 (
    .out0(mul), .out1(decoder_5_out1), .out2(div), .out3(decoder_5_out3), .out4(mulu), .out5(decoder_5_out5),
    .out6(divu), .out7(decoder_5_out7), .sel(buffer_1_out), .en(decoder_1_out6));
  or or_6 (or_6_out, decoder_3_out4, decoder_3_out3, decoder_3_out1, decoder_3_out5, decoder_3_out7);
  or or_7 (or_7_out, or_8_out, decoder_5_out1);
  or or_8 (or_8_out, decoder_5_out7, decoder_5_out5, decoder_5_out3);
endmodule

module Decoder_Inmediate (
  input  Enable,
  input  a,
  input  b,
  input  c,
  input  d,
  input  e,
  input  f,
  output Invalid,
  output Branch,
  output lw,
  output sw,
  output addi,
  output andi,
  output ori,
  output xori,
  output slti,
  output sltui,
  output SE
);

  wire and_1_out, decoder_1_out1, decoder_1_out2, decoder_1_out3, decoder_1_out4, decoder_1_out5,
       decoder_1_out6, decoder_1_out7, decoder_2_out1, decoder_2_out7, nand_1_out, or_1_out, or_2_out;

  Decoder_part #(.select(3), .disabled(0)) decoder_1 (
    .out0(Branch), .out1(decoder_1_out1), .out2(decoder_1_out2), .out3(decoder_1_out3),
    .out4(decoder_1_out4), .out5(decoder_1_out5), .out6(decoder_1_out6), .out7(decoder_1_out7),
    .sel({c, b, a}), .en(Enable));
  Decoder_part #(.select(3), .disabled(0)) decoder_2 (
    .out0(addi), .out1(decoder_2_out1), .out2(slti), .out3(sltui), .out4(andi), .out5(ori), .out6(xori),
    .out7(decoder_2_out7), .sel({d, e, f}), .en(decoder_1_out4));
  nor nor_1 (SE, andi, ori, xori);
  or or_1 (or_1_out, decoder_1_out1, decoder_1_out5);
  nand nand_1 (nand_1_out, f, e, ~d);  // NAND_Gate
  or or_2 (or_2_out, and_1_out, decoder_2_out1, decoder_2_out7);
  and and_1 (and_1_out, or_1_out, nand_1_out);
  or or_3 (Invalid, decoder_1_out2, decoder_1_out3, decoder_1_out6, decoder_1_out7, or_2_out);
  and and_2 (lw, decoder_1_out1, ~and_1_out);  // AND_Gate
  and and_3 (sw, decoder_1_out5, ~and_1_out);  // AND_Gate
endmodule

module Decoder_Opcode (
  input  a,
  input  b,
  input  c,
  input  d,
  input  e,
  input  f,
  output Invalid,
  output Function,
  output Special,
  output Stack,
  output Jump,
  output Inmediate
);

  wire and_1_out, and_2_out, and_3_out, and_4_out, and_5_out, and_6_out, and_7_out, and_8_out, and_9_out,
       and_10_out, and_11_out, and_12_out, and_13_out, and_16_out, nand_1_out, nor_1_out, nor_2_out,
       not_1_out, not_2_out, not_3_out, not_4_out, not_5_out, not_6_out, not_7_out, not_8_out, not_9_out,
       or_1_out, or_2_out, or_3_out, or_4_out, or_5_out, xor_1_out;

  not not_1 (not_1_out, d);
  nand nand_1 (nand_1_out, d, e);
  and and_1 (and_1_out, a, b, c);
  nor nor_1 (nor_1_out, a, b, c);
  not not_2 (not_2_out, d);
  and and_2 (and_2_out, d, e, f);
  nor nor_2 (nor_2_out, d, e, f);
  not not_3 (not_3_out, f);
  not not_4 (not_4_out, e);
  not not_5 (not_5_out, f);
  not not_6 (not_6_out, a);
  or or_1 (or_1_out, and_1_out, nor_1_out);
  or or_2 (or_2_out, and_2_out, nor_2_out);
  and and_3 (and_3_out, not_2_out, not_3_out, e);
  or or_3 (or_3_out, d, and_4_out);
  and and_4 (and_4_out, not_1_out, not_4_out, f);
  and and_5 (and_5_out, not_1_out, e, f);
  not not_7 (not_7_out, b);
  and and_6 (and_6_out, and_5_out, not_7_out, a);
  and and_7 (and_7_out, not_7_out, not_8_out, c);
  not not_8 (not_8_out, a);
  xor xor_1 (xor_1_out, e, f);
  and and_8 (and_8_out, not_6_out, or_1_out);
  and and_9 (and_9_out, a, or_2_out, or_1_out);
  and and_10 (and_10_out, not_2_out, or_2_out);
  and and_11 (and_11_out, d, or_2_out);
  and and_12 (and_12_out, and_7_out, nand_1_out, not_5_out);
  and and_13 (and_13_out, d, and_7_out, xor_1_out);
  and and_14 (Function, and_8_out, and_10_out);
  not not_9 (not_9_out, and_11_out);
  and and_15 (Jump, and_8_out, and_3_out);
  and and_16 (and_16_out, and_8_out, or_3_out);
  or or_4 (or_4_out, and_9_out, Function);
  and and_17 (Special, and_9_out, and_11_out);
  and and_18 (Stack, and_9_out, not_9_out);
  or or_5 (or_5_out, and_16_out, and_6_out, and_12_out);
  or or_6 (Inmediate, or_5_out, and_13_out);
  nor nor_3 (Invalid, or_4_out, Inmediate, Jump);
endmodule

module Decoder_Specials (
  input  Enable,
  input  a,
  input  b,
  input  c,
  input  d,
  input  e,
  input  f,
  output Invalid,
  output halt,
  output kbd,
  output rnd,
  output tty
);

  wire and_1_out, and_2_out, and_3_out, and_4_out, and_5_out, and_6_out, and_7_out, and_8_out, and_9_out,
       and_13_out, and_14_out, and_15_out, nor_1_out, nor_2_out, or_1_out, or_2_out, or_3_out, xnor_1_out;

  and and_1 (and_1_out, a, Enable);
  and and_2 (and_2_out, b, Enable);
  and and_3 (and_3_out, c, Enable);
  and and_4 (and_4_out, d, Enable);
  and and_5 (and_5_out, e, Enable);
  and and_6 (and_6_out, f, Enable);
  and and_7 (and_7_out, and_1_out, and_2_out, and_3_out);
  nor nor_1 (nor_1_out, and_1_out, and_2_out, and_3_out);
  and and_8 (and_8_out, and_4_out, and_5_out, and_6_out);
  nor nor_2 (nor_2_out, and_4_out, and_5_out, and_6_out);
  NotExactlyOne xnor_1 (.out(xnor_1_out), .in0(and_4_out), .in1(and_5_out), .in2(and_6_out));
  or or_1 (or_1_out, xnor_1_out, nor_2_out, ~nor_1_out, and_8_out, and_7_out);  // OR_Gate
  and and_9 (and_9_out, nor_1_out, or_1_out);
  and and_10 (kbd, ~or_1_out, and_4_out);  // AND_Gate
  and and_11 (rnd, ~or_1_out, and_5_out);  // AND_Gate
  and and_12 (tty, ~or_1_out, and_6_out);  // AND_Gate
  or or_2 (or_2_out, and_9_out, or_3_out);
  or or_3 (or_3_out, and_13_out, and_14_out, and_15_out);
  and and_13 (and_13_out, and_7_out, ~and_8_out);  // AND_Gate
  and and_14 (and_14_out, and_7_out, ~and_8_out);  // AND_Gate
  and and_15 (and_15_out, or_1_out, ~and_7_out);  // AND_Gate
  and and_16 (Invalid, Enable, or_2_out);
  and and_17 (halt, ~or_2_out, and_7_out);  // AND_Gate
endmodule

module Decoder_Stack (
  input  Enable,
  input  d,
  input  e,
  input  f,
  output Invalid,
  output pop,
  output push
);

  wire and_1_out, or_1_out;

  or or_1 (or_1_out, d, e);
  and and_1 (and_1_out, ~or_1_out, Enable);  // AND_Gate
  Decoder_part #(.disabled(0)) decoder_1 (.out0(pop), .out1(push), .sel(f), .en(and_1_out));
  and and_2 (Invalid, Enable, or_1_out);
endmodule

module Decoder (
  input  Clock,
  input  Ready,
  input  [31:0] R1,
  input  [31:0] R2,
  input  [31:0] IO_Input,
  input  Reset,
  input  [31:0] HiLo_read,
  input  [31:0] SP_IN,
  input  [31:0] Result_1,
  input  [31:0] Result_2,
  input  Condition,
  output Invalid,
  output Halt,
  output [3:0] IO_Code,
  output [31:0] IO_Address,
  output [31:0] R3,
  output [31:0] IO_Output,
  output [4:0] S_R1,
  output [4:0] S_R2,
  output [4:0] S_R3,
  output R_Write,
  output [31:0] R4,
  output HiLo_write,
  output HiLo_select,
  output [31:0] SP_OUT,
  output [3:0] ALU_code,
  output Activate_ALU,
  output [31:0] OP1,
  output [31:0] OP2,
  output SP_write
);

  wire and_1_out, and_2_out, and_3_out, and_5_out, and_6_out, and_7_out, decoder_branch_1_beq,
       decoder_branch_1_bgtz, decoder_branch_1_blez, decoder_branch_1_bltz, decoder_branch_1_bne,
       decoder_branch_1_invalid, decoder_functions_1_add, decoder_functions_1_and, decoder_functions_1_div,
       decoder_functions_1_divu, decoder_functions_1_invalid, decoder_functions_1_jr,
       decoder_functions_1_mflo, decoder_functions_1_mul, decoder_functions_1_mulu, decoder_functions_1_nor,
       decoder_functions_1_or, decoder_functions_1_slt, decoder_functions_1_sltu, decoder_functions_1_sub,
       decoder_functions_1_xor, decoder_inmediate_1_addi, decoder_inmediate_1_andi,
       decoder_inmediate_1_branch, decoder_inmediate_1_invalid, decoder_inmediate_1_lw,
       decoder_inmediate_1_ori, decoder_inmediate_1_se, decoder_inmediate_1_slti, decoder_inmediate_1_sltui,
       decoder_inmediate_1_sw, decoder_inmediate_1_xori, decoder_opcode_1_function,
       decoder_opcode_1_inmediate, decoder_opcode_1_invalid, decoder_opcode_1_special,
       decoder_opcode_1_stack, decoder_specials_1_invalid, decoder_stack_1_invalid, Imm, iom, ior, iow, kbd,
       NXT, or_1_out, or_3_out, or_10_out, or_11_out, or_12_out, or_13_out, or_14_out, or_15_out, or_16_out,
       pop, push, rnd, SignExt, tty, xor_1_out;
  wire [1:0] decoder_opcode_1_jump, or_18_out;
  wire [7:2] register_2_q;
  wire [17:2] Jumpoff;
  wire [31:0] adder_1_out, adder_2_out, adder_3_out, ioa, ip, mul4_1_output, multiplexer_2_out,
       multiplexer_3_out, multiplexer_5_out, multiplexer_6_out, multiplexer_7_out, multiplexer_11_out,
       register_3_q, signextend_1_data_2;

  or or_1 (or_1_out, tty, rnd, kbd, iom);
  Priority_Encoder #(.disabled(0)) priority_encoder_1 (
    .in0(1'b1), .in1(iow), .in2(tty), .in3(kbd), .in4(rnd), .in5(1'b0), .in6(1'b0), .in7(1'b0),
    .out(IO_Code[2:0]));  // open: en_in
  Multiplexer #(.width(32), .disabled(0), .enable("false")) multiplexer_1 (
    .in0(ip), .in1(ioa), .out(IO_Address), .sel(iom));
  Multiplexer #(.select(2), .width(32), .enable("false")) multiplexer_2 (
    .in0(adder_1_out), .in1({ip[31:28], S_R1, S_R2, Jumpoff, 2'b00}), .in2(multiplexer_5_out), .in3(32'h4),
    .out(multiplexer_2_out), .sel(decoder_opcode_1_jump));
  or or_2 (SP_write, pop, push);
  and and_1 (and_1_out, Ready, ~and_2_out);  // AND_Gate
  and and_2 (and_2_out, Ready, or_1_out);
  and and_3 (and_3_out, Ready, ~or_1_out);  // AND_Gate
  or or_3 (or_3_out, Ready, ~or_1_out);  // OR_Gate
  Register #(.width(32)) register_1 (.D(multiplexer_2_out), .en(NXT), .Q(ip), .clk(Clock), .clr(Reset));
  Multiplexer #(.width(32), .disabled(0), .enable("false")) multiplexer_3 (
    .in0({32{1'b0}}), .in1(IO_Input), .out(multiplexer_3_out), .sel(and_1_out));
  D_Flip_Flop #(.trigger("falling")) d_ff_1 (
    .clk(Clock), .D(and_3_out), .Q(NXT), .reset(Reset));  // open: Qn, preset, en
  Multiplexer #(.select(3), .width(32), .enable("false")) multiplexer_4 (
    .in0({32{1'b0}}), .in1(multiplexer_11_out), .in2(R1), .in3({32{1'b0}}), .in4({32{1'b0}}),
    .in5({32{1'b0}}), .in6({32{1'b0}}), .in7({32{1'b0}}), .out(IO_Output), .sel(IO_Code[2:0]));
  Adder #(.width(32)) adder_1 (.a(ip), .b(32'h4), .out(adder_1_out));  // open: cin, cout
  Multiplexer #(.width(32), .disabled(0), .enable("false")) multiplexer_5 (
    .in0(adder_2_out), .in1(R1), .out(multiplexer_5_out), .sel(decoder_functions_1_jr));
  Mul4 mul4_1 (.Input(signextend_1_data_2), .Output(mul4_1_output));
  Register #(.width(32), .trigger("falling")) register_2 (
    .D(multiplexer_3_out), .en(or_3_out),
    .Q({Jumpoff[9:2], Jumpoff[17:10], S_R1[2:0], S_R2, register_2_q, S_R1[4:3]}), .clk(Clock), .clr(Reset));
  and and_4 (Imm, ~decoder_inmediate_1_branch, decoder_opcode_1_inmediate);  // AND_Gate
  or or_4 (Invalid, decoder_opcode_1_invalid, decoder_inmediate_1_invalid, decoder_branch_1_invalid, decoder_functions_1_invalid, decoder_specials_1_invalid, decoder_stack_1_invalid);
  Adder #(.width(32)) adder_2 (.a(mul4_1_output), .b(adder_1_out), .out(adder_2_out));  // open: cin, cout
  or or_5 (iow, push, decoder_inmediate_1_sw);
  or or_6 (iom, iow, ior);
  or or_7 (ior, pop, decoder_inmediate_1_lw);
  Decoder_Opcode decoder_opcode_1 (
    .a(register_2_q[7]), .b(register_2_q[6]), .c(register_2_q[5]), .d(register_2_q[4]), .e(register_2_q[3]),
    .f(register_2_q[2]), .Invalid(decoder_opcode_1_invalid), .Function(decoder_opcode_1_function),
    .Special(decoder_opcode_1_special), .Stack(decoder_opcode_1_stack), .Jump(decoder_opcode_1_jump[0]),
    .Inmediate(decoder_opcode_1_inmediate));
  Adder #(.width(32)) adder_3 (.a(signextend_1_data_2), .b(R1), .out(adder_3_out));  // open: cin, cout
  or or_8 (decoder_opcode_1_jump[1], xor_1_out, decoder_functions_1_jr);
  Decoder_Inmediate decoder_inmediate_1 (
    .Enable(decoder_opcode_1_inmediate), .a(register_2_q[7]), .b(register_2_q[6]), .c(register_2_q[5]),
    .d(register_2_q[4]), .e(register_2_q[3]), .f(register_2_q[2]), .SE(decoder_inmediate_1_se),
    .Invalid(decoder_inmediate_1_invalid), .Branch(decoder_inmediate_1_branch), .lw(decoder_inmediate_1_lw),
    .sw(decoder_inmediate_1_sw), .addi(decoder_inmediate_1_addi), .andi(decoder_inmediate_1_andi),
    .ori(decoder_inmediate_1_ori), .xori(decoder_inmediate_1_xori), .slti(decoder_inmediate_1_slti),
    .sltui(decoder_inmediate_1_sltui));
  xor xor_1 (xor_1_out, decoder_branch_1_bne, Condition);
  Multiplexer #(.width(32), .disabled(0), .enable("false")) multiplexer_6 (
    .in0(32'hfffffffc), .in1(32'h4), .out(multiplexer_6_out), .sel(pop));
  Decoder_Branch decoder_branch_1 (
    .d(register_2_q[4]), .e(register_2_q[3]), .f(register_2_q[2]), .Invalid(decoder_branch_1_invalid),
    .bltz(decoder_branch_1_bltz), .beq(decoder_branch_1_beq), .bne(decoder_branch_1_bne),
    .blez(decoder_branch_1_blez), .bgtz(decoder_branch_1_bgtz), .Enable(decoder_inmediate_1_branch));
  Register #(.width(32)) register_3 (.D(SP_IN), .Q(register_3_q), .clk(SP_write));  // open: en, clr
  or or_9 (SignExt, decoder_inmediate_1_se, decoder_inmediate_1_branch);
  Adder #(.width(32)) adder_4 (.a(register_3_q), .b(multiplexer_6_out), .out(SP_OUT));  // open: cin, cout
  Decoder_Functions decoder_functions_1 (
    .Enable(decoder_opcode_1_function), .a(Jumpoff[7]), .b(Jumpoff[6]), .c(Jumpoff[5]), .d(Jumpoff[4]),
    .e(Jumpoff[3]), .f(Jumpoff[2]), .Invalid(decoder_functions_1_invalid), .add(decoder_functions_1_add),
    .sub(decoder_functions_1_sub), .\and (decoder_functions_1_and), .\or (decoder_functions_1_or),
    .\nor (decoder_functions_1_nor), .\xor (decoder_functions_1_xor), .mul(decoder_functions_1_mul),
    .mulu(decoder_functions_1_mulu), .div(decoder_functions_1_div), .divu(decoder_functions_1_divu),
    .slt(decoder_functions_1_slt), .sltu(decoder_functions_1_sltu), .mfhi(HiLo_select),
    .mflo(decoder_functions_1_mflo), .jr(decoder_functions_1_jr));
  Multiplexer #(.width(32), .disabled(0), .enable("false")) multiplexer_7 (
    .in0(SP_OUT), .in1(register_3_q), .out(multiplexer_7_out), .sel(pop));
  Decoder_Specials decoder_specials_1 (
    .Enable(decoder_opcode_1_special), .a(Jumpoff[7]), .b(Jumpoff[6]), .c(Jumpoff[5]), .d(Jumpoff[4]),
    .e(Jumpoff[3]), .f(Jumpoff[2]), .Invalid(decoder_specials_1_invalid), .halt(Halt), .kbd(kbd), .rnd(rnd),
    .tty(tty));
  or or_10 (or_10_out, decoder_functions_1_add, decoder_inmediate_1_addi);
  or or_11 (or_11_out, decoder_functions_1_and, decoder_inmediate_1_andi);
  or or_12 (or_12_out, decoder_functions_1_or, decoder_inmediate_1_ori);
  or or_13 (or_13_out, decoder_functions_1_xor, decoder_inmediate_1_xori);
  or or_14 (or_14_out, decoder_functions_1_slt, decoder_inmediate_1_slti);
  or or_15 (or_15_out, decoder_functions_1_sltu, decoder_inmediate_1_sltui);
  or or_16 (or_16_out, decoder_branch_1_beq, decoder_branch_1_bne);
  Multiplexer #(.width(32), .disabled(0), .enable("false")) multiplexer_8 (
    .in0(adder_3_out), .in1(multiplexer_7_out), .out(ioa), .sel(SP_write));
  Decoder_Stack decoder_stack_1 (
    .Enable(decoder_opcode_1_stack), .d(Jumpoff[4]), .e(Jumpoff[3]), .f(Jumpoff[2]),
    .Invalid(decoder_stack_1_invalid), .pop(pop), .push(push));
  // Priority_Encoder #(.select(4), .disabled(0)) priority_encoder_2: pin names not known; wires that end beside it: or_10_out, decoder_functions_1_sub, or_11_out, or_12_out, decoder_functions_1_nor, or_13_out, decoder_functions_1_mul, decoder_functions_1_mulu, ALU_code, decoder_functions_1_div, Activate_ALU, decoder_functions_1_divu, or_14_out, or_15_out, or_16_out, decoder_branch_1_blez, decoder_branch_1_bgtz, decoder_branch_1_bltz
  and and_5 (and_5_out, Activate_ALU, ~or_16_out, ~decoder_branch_1_blez, ~decoder_branch_1_bgtz, ~decoder_branch_1_bltz);  // AND_Gate
  or or_17 (HiLo_write, decoder_functions_1_mul, decoder_functions_1_mulu, decoder_functions_1_div, decoder_functions_1_divu);
  Multiplexer #(.width(5), .disabled(0), .enable("false")) multiplexer_9 (
    .in0(Jumpoff[17:13]), .in1(S_R2), .out(S_R3), .sel(Imm));
  Multiplexer #(.width(32), .disabled(0), .enable("false")) multiplexer_10 (
    .in0(R2), .in1(signextend_1_data_2), .out(OP2), .sel(Imm));
  and and_6 (and_6_out, Ready, ior);
  and and_7 (and_7_out, and_5_out, ~HiLo_write);  // AND_Gate
  SignExtend signextend_1 (.Data(Jumpoff), .Sign(SignExt), .Data_2(signextend_1_data_2));
  or or_18 (or_18_out[0], kbd, rnd, and_6_out);
  or or_19 (or_18_out[1], decoder_functions_1_mflo, HiLo_select);
  Multiplexer #(.width(32), .disabled(0), .enable("false")) multiplexer_11 (
    .in0(R2), .in1(R1), .out(multiplexer_11_out), .sel(push));
  Multiplexer #(.select(2), .width(32), .disabled(0), .enable("false")) multiplexer_12 (
    .in0(Result_1), .in1(IO_Input), .in2(HiLo_read), .in3(Result_1), .out(R3), .sel(or_18_out));
  or or_20 (R_Write, and_7_out, or_18_out[1], or_18_out[0]);

  assign IO_Code[3] = 1'b0;
  assign OP1 = R1;
  assign R4 = Result_2;

  // Other names for the same wires on the sheet: CLK = Clock; IOIN[31:0] = IO_Input;
  //   Jumpoff[31:18] = {ip[31:28], S_R1, S_R2}; RDY = Ready; RST = Reset; stack = SP_write

  // Notes on the sheet:
  //   Rs
  //   Rt
  //   Rd
  //   Constant
endmodule

module Fetcher_Last (
  input  Clock,
  input  Write,
  input  [15:0] Data,
  input  Fill,
  output [15:0] Output
);

  wire or_1_out, or_2_out;
  wire [15:0] multiplexer_1_out;

  or or_1 (or_1_out, Clock, Fill);
  or or_2 (or_2_out, Write, Fill);
  Multiplexer #(.width(16), .enable("false")) multiplexer_1 (
    .in0(Data), .in1({16{1'b1}}), .out(multiplexer_1_out), .sel(Fill));
  Register #(.width(16), .trigger("high")) register_1 (
    .D(multiplexer_1_out), .en(or_2_out), .Q(Output), .clk(or_1_out));  // open: clr
endmodule

module Fetcher_Load (
  input  Clock,
  input  [31:0] Block_0,
  input  [31:0] Block_1,
  input  [31:0] Block_2,
  input  [31:0] Block_3,
  input  Write,
  output [31:0] Block_0_2,
  output [31:0] Block_1_2,
  output [31:0] Block_2_2,
  output [31:0] Block_3_2
);

  Register #(.width(32)) register_1 (.D(Block_0), .en(Write), .Q(Block_0_2), .clk(Clock));  // open: clr
  Register #(.width(32)) register_2 (.D(Block_1), .en(Write), .Q(Block_1_2), .clk(Clock));  // open: clr
  Register #(.width(32)) register_3 (.D(Block_2), .en(Write), .Q(Block_2_2), .clk(Clock));  // open: clr
  Register #(.width(32)) register_4 (.D(Block_3), .en(Write), .Q(Block_3_2), .clk(Clock));  // open: clr
endmodule

module IO_Bridge (
  input  Clock,
  input  [3:0] Code,
  input  Reset,
  input  [31:0] RAM0_Read,
  input  [31:0] RAM1_Read,
  input  [31:0] RAM2_Read,
  input  [31:0] Address,
  input  [31:0] RAM3_Read,
  input  [31:0] Input,
  input  [3:0] Read_Time,
  input  [3:0] Write_Time,
  input  [6:0] KBD_Data,
  input  KBD_Avail,
  output [31:0] RAM0_Write,
  output [31:0] Output,
  output [31:0] RAM1_Write,
  output [31:0] RAM2_Write,
  output Ready,
  output [31:0] RAM3_Write,
  output [15:0] RAM_Address,
  output [3:0] Write_Mask,
  output RAM_ON,
  output RAM_R_W,
  output KBD_On,
  output [6:0] TTY_Data,
  output TTY_On
);

  wire and_1_out, comparator_1_eq, comparator_2_gt, comparator_3_gt, counter_1_carry, counter_2_carry,
       decoder_2_out0, decoder_2_out4, not_1_out, not_2_out, or_1_out, or_2_out, or_3_out, or_4_out, or_5_out;
  wire [3:0] counter_1_q, counter_2_q;
  wire [6:0] multiplexer_7_out;
  wire [15:0] fetcher_last_1_output;
  wire [31:0] fetcher_load_1_block_0_2, fetcher_load_1_block_1_2, fetcher_load_1_block_2_2,
       fetcher_load_1_block_3_2, multiplexer_6_out, random_1_out;

  Fetcher_Load fetcher_load_1 (
    .Clock(Clock), .Block_0(RAM0_Read), .Block_1(RAM1_Read), .Block_2(RAM2_Read), .Block_3(RAM3_Read),
    .Write(not_1_out), .Block_0_2(fetcher_load_1_block_0_2), .Block_1_2(fetcher_load_1_block_1_2),
    .Block_2_2(fetcher_load_1_block_2_2), .Block_3_2(fetcher_load_1_block_3_2));
  Multiplexer #(.disabled(0), .enable("false")) multiplexer_1 (
    .in0(not_1_out), .in1(not_2_out), .out(RAM_ON), .sel(RAM_R_W));
  Multiplexer #(.width(32), .disabled(0), .enable("false")) multiplexer_2 (
    .in0({32{1'b0}}), .in1(Input), .out(RAM0_Write), .sel(Write_Mask[0]));
  Multiplexer #(.width(32), .disabled(0), .enable("false")) multiplexer_3 (
    .in0({32{1'b0}}), .in1(Input), .out(RAM1_Write), .sel(Write_Mask[1]));
  Multiplexer #(.width(32), .disabled(0), .enable("false")) multiplexer_4 (
    .in0({32{1'b0}}), .in1(Input), .out(RAM2_Write), .sel(Write_Mask[2]));
  Multiplexer #(.width(32), .disabled(0), .enable("false")) multiplexer_5 (
    .in0({32{1'b0}}), .in1(Input), .out(RAM3_Write), .sel(Write_Mask[3]));
  or or_1 (or_1_out, ~RAM_R_W, Reset);  // OR_Gate
  or or_2 (or_2_out, and_1_out, Reset);
  Fetcher_Last fetcher_last_1 (
    .Clock(Clock), .Write(or_5_out), .Data(Address[19:4]), .Fill(or_2_out), .Output(fetcher_last_1_output));
  Multiplexer #(.select(2), .width(32), .disabled(0), .enable("false")) multiplexer_6 (
    .in0(fetcher_load_1_block_0_2), .in1(fetcher_load_1_block_1_2), .in2(fetcher_load_1_block_2_2),
    .in3(fetcher_load_1_block_3_2), .out(multiplexer_6_out), .sel(Address[3:2]));
  or or_3 (or_3_out, comparator_1_eq, ~decoder_2_out0, Reset);  // OR_Gate
  not not_1 (not_1_out, comparator_1_eq);
  not not_2 (not_2_out, or_4_out);
  Counter #(.width(4), .max('hf)) counter_1 (
    .Q(counter_1_q), .carry(counter_1_carry), .clk(Clock), .clr(or_1_out));  // open: load, D, count
  Comparator #(.width(16), .mode("unsigned")) comparator_1 (
    .a(fetcher_last_1_output), .b(Address[19:4]), .eq(comparator_1_eq));  // open: gt, lt
  Counter #(.width(4), .max('hf)) counter_2 (
    .Q(counter_2_q), .carry(counter_2_carry), .clk(Clock), .clr(or_3_out));  // open: load, D, count
  Decoder_part #(.select(2), .disabled(0), .enable("false")) decoder_1 (
    .out0(Write_Mask[0]), .out1(Write_Mask[1]), .out2(Write_Mask[2]), .out3(Write_Mask[3]), .sel(Address[3:2]));
  or or_4 (or_4_out, counter_1_carry, comparator_2_gt);
  Comparator #(.width(4), .mode("unsigned")) comparator_2 (
    .a(counter_1_q), .b(Write_Time), .gt(comparator_2_gt));  // open: eq, lt
  or or_5 (or_5_out, counter_2_carry, comparator_3_gt);
  and and_1 (and_1_out, comparator_1_eq, RAM_R_W);
  Comparator #(.width(4), .mode("unsigned")) comparator_3 (
    .a(counter_2_q), .b(Read_Time), .gt(comparator_3_gt));  // open: eq, lt
  Random #(.width(32)) random_1 (.clk(Clock), .out(random_1_out));  // open: next, clr
  Multiplexer #(.width(7), .disabled(0)) multiplexer_7 (
    .in0({7{1'b1}}), .in1(KBD_Data), .out(multiplexer_7_out), .sel(KBD_Avail), .en(KBD_On));
  Decoder_part #(.select(4), .disabled(0), .enable("false")) decoder_2 (
    .out0(decoder_2_out0), .out1(RAM_R_W), .out2(TTY_On), .out3(KBD_On), .out4(decoder_2_out4), .sel(Code));  // open: out5, out6, out7, out8, out9, out10, out11, out12, out13, out14, out15
  Multiplexer #(.select(4), .width(32), .disabled(0), .enable("false")) multiplexer_8 (
    .in0(multiplexer_6_out), .in1({32{1'b0}}), .in2({32{1'b0}}), .in3({{25{1'b0}}, multiplexer_7_out}),
    .in4(random_1_out), .in5({32{1'b0}}), .in6({32{1'b0}}), .in7({32{1'b0}}), .in8({32{1'b0}}),
    .in9({32{1'b0}}), .in10({32{1'b0}}), .in11({32{1'b0}}), .in12({32{1'b0}}), .in13({32{1'b0}}),
    .in14({32{1'b0}}), .in15({32{1'b0}}), .out(Output), .sel(Code));
  Multiplexer #(.select(4), .disabled(0), .enable("false")) multiplexer_9 (
    .in0(comparator_1_eq), .in1(or_4_out), .in2(TTY_On), .in3(KBD_On), .in4(decoder_2_out4), .in5(1'b0),
    .in6(1'b0), .in7(1'b0), .in8(1'b0), .in9(1'b0), .in10(1'b0), .in11(1'b0), .in12(1'b0), .in13(1'b0),
    .in14(1'b0), .in15(1'b0), .out(Ready), .sel(Code));

  assign RAM_Address = Address[19:4];
  assign TTY_Data = Input[6:0];
endmodule

module Mul4 (
  input  [31:0] Input,
  output [31:0] Output
);

  wire [31:0] alu_2complement_1_result, alu_2complement_2_result, multiplexer_1_out;

  ALU_2Complement alu_2complement_1 (.OP(Input), .Result(alu_2complement_1_result));
  Multiplexer #(.width(32), .disabled(0), .enable("false")) multiplexer_1 (
    .in0(Input), .in1(alu_2complement_1_result), .out({{2{multiplexer_1_out[31]}}, multiplexer_1_out[29:0]}),
    .sel(Input[31]));
  Multiplexer #(.width(32), .disabled(0), .enable("false")) multiplexer_2 (
    .in0({multiplexer_1_out[29:0], 2'b00}), .in1(alu_2complement_2_result), .out(Output), .sel(Input[31]));
  ALU_2Complement alu_2complement_2 (.OP({multiplexer_1_out[29:0], 2'b00}), .Result(alu_2complement_2_result));
  // also tied to GND on the sheet: multiplexer_1_out[31]
endmodule

module RegistryFile (
  input  Clock,
  input  [4:0] S_R1,
  input  [31:0] SP_IN,
  input  SP_write,
  input  [4:0] S_R2,
  input  [4:0] Modify,
  input  [31:0] New_Value,
  input  Write,
  input  Reset,
  input  [31:0] R4,
  input  Write_HiLo,
  input  Select_HiLo,
  output [31:0] R1,
  output [31:0] R2,
  output [31:0] SP_OUT,
  output [31:0] HiLo_output
);

  wire and_1_out, and_2_out, decoder_1_out0, decoder_1_out1, decoder_1_out2, decoder_1_out3, decoder_1_out4,
       decoder_1_out5, decoder_1_out6, decoder_1_out7, decoder_1_out8, decoder_1_out9, decoder_1_out10,
       decoder_1_out11, decoder_1_out12, decoder_1_out13, decoder_1_out14, decoder_1_out15, decoder_1_out16,
       decoder_1_out17, decoder_1_out18, decoder_1_out19, decoder_1_out20, decoder_1_out21, decoder_1_out22,
       decoder_1_out23, decoder_1_out24, decoder_1_out25, decoder_1_out26, decoder_1_out27, decoder_1_out28,
       decoder_1_out29, decoder_1_out30, decoder_1_out31, or_1_out;
  wire [31:0] adder_1_out, multiplexer_2_out, multiplexer_3_out, register_1_q, register_2_q, register_3_q,
       register_4_q, register_5_q, register_6_q, register_7_q, register_8_q, register_9_q, register_10_q,
       register_11_q, register_12_q, register_13_q, register_14_q, register_15_q, register_16_q,
       register_17_q, register_18_q, register_19_q, register_20_q, register_21_q, register_22_q,
       register_23_q, register_24_q, register_25_q, register_26_q, register_27_q, register_28_q,
       register_29_q, register_30_q, register_31_q, register_32_q, register_33_q;

  Register #(.width(32), .trigger("falling")) register_1 (
    .D(R4), .en(Write_HiLo), .Q(register_1_q), .clk(Clock), .clr(Reset));
  Register #(.width(32), .trigger("falling")) register_2 (
    .D(New_Value), .en(Write_HiLo), .Q(register_2_q), .clk(Clock), .clr(Reset));
  Multiplexer #(.width(32), .disabled(0), .enable("false")) multiplexer_1 (
    .in0(register_2_q), .in1(register_1_q), .out(HiLo_output), .sel(Select_HiLo));
  Decoder_part #(.select(5), .disabled(0)) decoder_1 (
    .out0(decoder_1_out0), .out1(decoder_1_out1), .out2(decoder_1_out2), .out3(decoder_1_out3),
    .out4(decoder_1_out4), .out5(decoder_1_out5), .out6(decoder_1_out6), .out7(decoder_1_out7),
    .out8(decoder_1_out8), .out9(decoder_1_out9), .out10(decoder_1_out10), .out11(decoder_1_out11),
    .out12(decoder_1_out12), .out13(decoder_1_out13), .out14(decoder_1_out14), .out15(decoder_1_out15),
    .out16(decoder_1_out16), .out17(decoder_1_out17), .out18(decoder_1_out18), .out19(decoder_1_out19),
    .out20(decoder_1_out20), .out21(decoder_1_out21), .out22(decoder_1_out22), .out23(decoder_1_out23),
    .out24(decoder_1_out24), .out25(decoder_1_out25), .out26(decoder_1_out26), .out27(decoder_1_out27),
    .out28(decoder_1_out28), .out29(decoder_1_out29), .out30(decoder_1_out30), .out31(decoder_1_out31),
    .sel(Modify), .en(Write));
  Register #(.width(32), .trigger("falling")) register_3 (
    .D(New_Value), .en(decoder_1_out0), .Q(register_3_q), .clr(Reset));  // open: clk
  Register #(.width(32), .trigger("falling")) register_4 (
    .D(New_Value), .en(decoder_1_out1), .Q(register_4_q), .clk(Clock), .clr(Reset));
  Register #(.width(32), .trigger("falling")) register_5 (
    .D(New_Value), .en(decoder_1_out4), .Q(register_5_q), .clk(Clock), .clr(Reset));
  Register #(.width(32), .trigger("falling")) register_6 (
    .D(New_Value), .en(decoder_1_out5), .Q(register_6_q), .clk(Clock), .clr(Reset));
  Register #(.width(32), .trigger("falling")) register_7 (
    .D(New_Value), .en(decoder_1_out8), .Q(register_7_q), .clk(Clock), .clr(Reset));
  Register #(.width(32), .trigger("falling")) register_8 (
    .D(New_Value), .en(decoder_1_out9), .Q(register_8_q), .clk(Clock), .clr(Reset));
  Register #(.width(32), .trigger("falling")) register_9 (
    .D(New_Value), .en(decoder_1_out12), .Q(register_9_q), .clk(Clock), .clr(Reset));
  Register #(.width(32), .trigger("falling")) register_10 (
    .D(New_Value), .en(decoder_1_out13), .Q(register_10_q), .clk(Clock), .clr(Reset));
  Register #(.width(32), .trigger("falling")) register_11 (
    .D(New_Value), .en(decoder_1_out16), .Q(register_11_q), .clk(Clock), .clr(Reset));
  Register #(.width(32), .trigger("falling")) register_12 (
    .D(New_Value), .en(decoder_1_out17), .Q(register_12_q), .clk(Clock), .clr(Reset));
  Register #(.width(32), .trigger("falling")) register_13 (
    .D(New_Value), .en(decoder_1_out20), .Q(register_13_q), .clk(Clock), .clr(Reset));
  Register #(.width(32), .trigger("falling")) register_14 (
    .D(New_Value), .en(decoder_1_out21), .Q(register_14_q), .clk(Clock), .clr(Reset));
  Register #(.width(32), .trigger("falling")) register_15 (
    .D(New_Value), .en(decoder_1_out24), .Q(register_15_q), .clk(Clock), .clr(Reset));
  Register #(.width(32), .trigger("falling")) register_16 (
    .D(New_Value), .en(decoder_1_out25), .Q(register_16_q), .clk(Clock), .clr(Reset));
  Register #(.width(32), .trigger("falling")) register_17 (
    .D(New_Value), .en(decoder_1_out28), .Q(register_17_q), .clk(Clock), .clr(Reset));
  Register #(.width(32), .trigger("falling")) register_18 (
    .D(New_Value), .en(decoder_1_out29), .Q(register_18_q), .clk(Clock), .clr(Reset));
  Multiplexer #(.width(32), .disabled(0), .enable("false")) multiplexer_2 (
    .in0(multiplexer_3_out), .in1(SP_IN), .out(multiplexer_2_out), .sel(and_1_out));
  Multiplexer #(.width(32), .disabled(0), .enable("false")) multiplexer_3 (
    .in0(New_Value), .in1(adder_1_out), .out(multiplexer_3_out), .sel(and_2_out));
  Adder #(.width(32)) adder_1 (.a(New_Value), .b(32'h4), .out(adder_1_out));  // open: cin, cout
  Register #(.width(32), .trigger("falling")) register_19 (
    .D(New_Value), .en(decoder_1_out2), .Q(register_19_q), .clk(Clock), .clr(Reset));
  Register #(.width(32), .trigger("falling")) register_20 (
    .D(New_Value), .en(decoder_1_out3), .Q(register_20_q), .clk(Clock), .clr(Reset));
  Register #(.width(32), .trigger("falling")) register_21 (
    .D(New_Value), .en(decoder_1_out6), .Q(register_21_q), .clk(Clock), .clr(Reset));
  Register #(.width(32), .trigger("falling")) register_22 (
    .D(New_Value), .en(decoder_1_out7), .Q(register_22_q), .clk(Clock), .clr(Reset));
  Register #(.width(32), .trigger("falling")) register_23 (
    .D(New_Value), .en(decoder_1_out10), .Q(register_23_q), .clk(Clock), .clr(Reset));
  Register #(.width(32), .trigger("falling")) register_24 (
    .D(New_Value), .en(decoder_1_out11), .Q(register_24_q), .clk(Clock), .clr(Reset));
  Register #(.width(32), .trigger("falling")) register_25 (
    .D(New_Value), .en(decoder_1_out14), .Q(register_25_q), .clk(Clock), .clr(Reset));
  Register #(.width(32), .trigger("falling")) register_26 (
    .D(New_Value), .en(decoder_1_out15), .Q(register_26_q), .clk(Clock), .clr(Reset));
  Register #(.width(32), .trigger("falling")) register_27 (
    .D(New_Value), .en(decoder_1_out18), .Q(register_27_q), .clk(Clock), .clr(Reset));
  Register #(.width(32), .trigger("falling")) register_28 (
    .D(New_Value), .en(decoder_1_out19), .Q(register_28_q), .clk(Clock), .clr(Reset));
  Register #(.width(32), .trigger("falling")) register_29 (
    .D(New_Value), .en(decoder_1_out22), .Q(register_29_q), .clk(Clock), .clr(Reset));
  Register #(.width(32), .trigger("falling")) register_30 (
    .D(New_Value), .en(decoder_1_out23), .Q(register_30_q), .clk(Clock), .clr(Reset));
  Register #(.width(32), .trigger("falling")) register_31 (
    .D(New_Value), .en(decoder_1_out26), .Q(register_31_q), .clk(Clock), .clr(Reset));
  Register #(.width(32), .trigger("falling")) register_32 (
    .D(New_Value), .en(decoder_1_out27), .Q(register_32_q), .clk(Clock), .clr(Reset));
  Register #(.width(32), .trigger("falling")) register_33 (
    .D(New_Value), .en(decoder_1_out30), .Q(register_33_q), .clk(Clock), .clr(Reset));
  Register #(.width(32), .trigger("falling")) register_34 (
    .D(multiplexer_2_out), .en(or_1_out), .Q(SP_OUT), .clk(Clock), .clr(Reset));
  or or_1 (or_1_out, decoder_1_out31, SP_write);
  and and_1 (and_1_out, ~decoder_1_out31, or_1_out);  // AND_Gate
  and and_2 (and_2_out, decoder_1_out31, SP_write);
  Multiplexer #(.select(5), .width(32), .disabled(0), .enable("false")) multiplexer_4 (
    .in0(register_3_q), .in1(register_4_q), .in2(register_19_q), .in3(register_20_q), .in4(register_5_q),
    .in5(register_6_q), .in6(register_21_q), .in7(register_22_q), .in8(register_7_q), .in9(register_8_q),
    .in10(register_23_q), .in11(register_24_q), .in12(register_9_q), .in13(register_10_q),
    .in14(register_25_q), .in15(register_26_q), .in16(register_11_q), .in17(register_12_q),
    .in18(register_27_q), .in19(register_28_q), .in20(register_13_q), .in21(register_14_q),
    .in22(register_29_q), .in23(register_30_q), .in24(register_15_q), .in25(register_16_q),
    .in26(register_31_q), .in27(register_32_q), .in28(register_17_q), .in29(register_18_q),
    .in30(register_33_q), .in31(SP_OUT), .out(R1), .sel(S_R1));
  Multiplexer #(.select(5), .width(32), .disabled(0), .enable("false")) multiplexer_5 (
    .in0(register_3_q), .in1(register_4_q), .in2(register_19_q), .in3(register_20_q), .in4(register_5_q),
    .in5(register_6_q), .in6(register_21_q), .in7(register_22_q), .in8(register_7_q), .in9(register_8_q),
    .in10(register_23_q), .in11(register_24_q), .in12(register_9_q), .in13(register_10_q),
    .in14(register_25_q), .in15(register_26_q), .in16(register_11_q), .in17(register_12_q),
    .in18(register_27_q), .in19(register_28_q), .in20(register_13_q), .in21(register_14_q),
    .in22(register_29_q), .in23(register_30_q), .in24(register_15_q), .in25(register_16_q),
    .in26(register_31_q), .in27(register_32_q), .in28(register_17_q), .in29(register_18_q),
    .in30(register_33_q), .in31(SP_OUT), .out(R2), .sel(S_R2));
endmodule

module SignExtend (
  input  [15:0] Data,
  input  Sign,
  output [31:0] Data_2
);

  wire [31:0] multiplexer_1_out, or_1_out;

  assign or_1_out = {{16{1'b0}}, Data} | multiplexer_1_out;  // OR_Gate or_1, 32 bits wide
  Multiplexer #(.width(32), .disabled(0), .enable("false")) multiplexer_1 (
    .in0({32{1'b0}}), .in1(32'hffff0000), .out(multiplexer_1_out), .sel(Data[15]));
  Multiplexer #(.width(32), .disabled(0), .enable("false")) multiplexer_2 (
    .in0({{16{1'b0}}, Data}), .in1(or_1_out), .out(Data_2), .sel(Sign));
endmodule
